// Logisim project my_full_adder.circ as structural Verilog: 3 circuits, main circuit 8-Bit adder
module _8_Bit_adder (
  input  Zero_constant,
  input  Input_A,
  input  Input_B,
  input  in_4,
  input  in_5,
  input  in_6,
  input  in_7,
  input  in_8,
  input  in_9,
  input  in_10,
  input  in_11,
  input  in_12,
  input  in_13,
  input  in_14,
  input  in_15,
  input  in_16,
  input  in_17,
  output Outputs,
  output out_19,
  output out_20,
  output out_21,
  output out_22,
  output out_23,
  output out_24,
  output out_25
);

  wire _4_Bit_adder_c_out;

  _4_Bit_Adder _4_Bit_adder (
    .C_in(Zero_constant), .V00(Input_A), .V01(Input_B), .V10(in_4), .V11(in_5), .V20(in_6), .V21(in_7),
    .V30(in_8), .V31(in_9), .S0(Outputs), .S1(out_19), .S2(out_20), .S3(out_21), .C_out(_4_Bit_adder_c_out));
  _4_Bit_Adder _4_Bit_adder_2 (
    .C_in(_4_Bit_adder_c_out), .V00(in_11), .V01(in_10), .V10(in_13), .V11(in_12), .V20(in_15), .V21(in_14),
    .V30(in_16), .V31(in_16), .S0(out_22), .S1(out_23), .S2(out_24), .S3(out_25));  // open: C_out
endmodule

module Full_adder (
  input  A,
  input  B,
  input  C_in,
  output S,
  output C_out
);

  wire and_1_out, and_2_out, xor_1_out;

  xor xor_1 (xor_1_out, A, B);
  xor u_S (S, xor_1_out, C_in);
  and and_1 (and_1_out, xor_1_out, C_in);
  and and_2 (and_2_out, A, B);
  or u_C_out (C_out, and_1_out, and_2_out);
endmodule

module _4_Bit_Adder (
  input  C_in,
  input  V00,
  input  V01,
  input  V10,
  input  V11,
  input  V20,
  input  V21,
  input  V30,
  input  V31,
  output S0,
  output S1,
  output S2,
  output S3,
  output C_out
);

  wire full_adder_1_c_out, full_adder_2_c_out, full_adder_3_c_out;

  Full_adder full_adder_1 (.A(V00), .B(V01), .C_in(C_in), .S(S0), .C_out(full_adder_1_c_out));
  Full_adder full_adder_2 (.A(V10), .B(V11), .C_in(full_adder_1_c_out), .S(S1), .C_out(full_adder_2_c_out));
  Full_adder full_adder_3 (.A(V20), .B(V21), .C_in(full_adder_2_c_out), .S(S2), .C_out(full_adder_3_c_out));
  Full_adder full_adder_4 (.A(V30), .B(V31), .C_in(full_adder_3_c_out), .S(S3), .C_out(C_out));
endmodule
