// Logisim project my_multiplexer.circ as structural Verilog: 4 circuits, main circuit 16-1 Multiplexer
module _16_1_Multiplexer (
  input  W0,
  input  W1,
  input  W2,
  input  W3,
  input  S0,
  input  S1,
  input  S2,
  input  S3,
  input  S4,
  input  S5,
  input  S6,
  input  S7,
  input  S8,
  input  S9,
  input  S10,
  input  S11,
  input  S12,
  input  S13,
  input  S14,
  input  S15,
  output O
);

  wire n8_1_multiplexer_1_o, n8_1_multiplexer_2_o;

  _8_1_Multiplexer u_8_1_multiplexer_1 (
    .W0(W0), .W1(W1), .W2(W2), .S0(S0), .S1(S1), .S2(S2), .S3(S3), .S4(S4), .S5(S5), .S6(S6), .S7(S7),
    .O(n8_1_multiplexer_1_o));
  _8_1_Multiplexer u_8_1_multiplexer_2 (
    .W0(W0), .W1(W1), .W2(W2), .S0(S8), .S1(S9), .S2(S10), .S3(S11), .S4(S12), .S5(S13), .S6(S14), .S7(S15),
    .O(n8_1_multiplexer_2_o));
  _2_1_Multiplexer u_2_1_multiplexer_1 (.Selector(W3), .S0(n8_1_multiplexer_1_o), .S1(n8_1_multiplexer_2_o), .O(O));
endmodule

module _2_1_Multiplexer (
  input  Selector,
  input  S0,
  input  S1,
  output O
);

  wire and_1_out, and_2_out, not_1_out;

  not not_1 (not_1_out, Selector);
  and and_1 (and_1_out, not_1_out, S0);
  and and_2 (and_2_out, Selector, S1);
  or or_1 (O, and_1_out, and_2_out);
endmodule

module _4_1_Multiplexer (
  input  T0,
  input  T1,
  input  S0,
  input  S1,
  input  S2,
  input  S3,
  output O
);

  wire n2_1_multiplexer_1_o, n2_1_multiplexer_2_o;

  _2_1_Multiplexer u_2_1_multiplexer_1 (.Selector(T0), .S0(S0), .S1(S1), .O(n2_1_multiplexer_1_o));
  _2_1_Multiplexer u_2_1_multiplexer_2 (.Selector(T0), .S0(S2), .S1(S3), .O(n2_1_multiplexer_2_o));
  _2_1_Multiplexer u_2_1_multiplexer_3 (.Selector(T1), .S0(n2_1_multiplexer_1_o), .S1(n2_1_multiplexer_2_o), .O(O));
endmodule

module _8_1_Multiplexer (
  input  W0,
  input  W1,
  input  W2,
  input  S0,
  input  S1,
  input  S2,
  input  S3,
  input  S4,
  input  S5,
  input  S6,
  input  S7,
  output O
);

  wire n4_1_multiplexer_1_o, n4_1_multiplexer_2_o;

  _4_1_Multiplexer u_4_1_multiplexer_1 (.T0(W0), .T1(W1), .S0(S0), .S1(S1), .S2(S2), .S3(S3), .O(n4_1_multiplexer_1_o));
  _4_1_Multiplexer u_4_1_multiplexer_2 (.T0(W0), .T1(W1), .S0(S4), .S1(S5), .S2(S6), .S3(S7), .O(n4_1_multiplexer_2_o));
  _2_1_Multiplexer u_2_1_multiplexer_1 (.Selector(W2), .S0(n4_1_multiplexer_1_o), .S1(n4_1_multiplexer_2_o), .O(O));
endmodule
