// Logisim project AddSub32.circ as structural Verilog: 5 circuits, main circuit main
module main (
  input  [31:0] A,
  input  [31:0] B,
  input  Operator,
  output [31:0] Res,
  output Overflow
);

  wire n32bitadder_1_overflow, xnor_1_out, xor_1_out;
  wire [31:0] multiplexer_1_out, not_1_out;

  assign not_1_out = ~B;  // NOT_Gate not_1, 32 bits wide
  _32BitAdder u_32bitadder_1 (
    .A(A), .B(multiplexer_1_out), .C_in(Operator), .Res(Res), .Overflow(n32bitadder_1_overflow));
  Multiplexer #(.width(32)) multiplexer_1 (
    .in0(B), .in1(not_1_out), .out(multiplexer_1_out), .sel(Operator));  // open: en
  xnor xnor_1 (xnor_1_out, B[31], A[31]);
  xor xor_1 (xor_1_out, n32bitadder_1_overflow, Res[31]);
  and and_1 (Overflow, xnor_1_out, xor_1_out);
endmodule

module _1BitAdder (
  input  A,
  input  B,
  input  C_in,
  output S,
  output C_out
);

  wire and_1_out, and_2_out, xor_1_out;

  xor xor_1 (xor_1_out, A, B);
  xor u_S (S, xor_1_out, C_in);
  and and_1 (and_1_out, xor_1_out, C_in);
  and and_2 (and_2_out, A, B);
  or u_C_out (C_out, and_1_out, and_2_out);
endmodule

module _4BitAdder (
  input  [3:0] A,
  input  [3:0] B,
  input  C_in,
  output [3:0] Res,
  output C_out
);

  wire n1bitadder_2_c_out, n1bitadder_3_c_out, n1bitadder_4_c_out;

  _1BitAdder u_1bitadder_1 (.A(A[3]), .B(B[3]), .C_in(n1bitadder_2_c_out), .S(Res[3]), .C_out(C_out));
  _1BitAdder u_1bitadder_2 (.A(A[2]), .B(B[2]), .C_in(n1bitadder_3_c_out), .S(Res[2]), .C_out(n1bitadder_2_c_out));
  _1BitAdder u_1bitadder_3 (.A(A[1]), .B(B[1]), .C_in(n1bitadder_4_c_out), .S(Res[1]), .C_out(n1bitadder_3_c_out));
  _1BitAdder u_1bitadder_4 (.A(A[0]), .B(B[0]), .C_in(C_in), .S(Res[0]), .C_out(n1bitadder_4_c_out));
endmodule

module _8BitAdder (
  input  [7:0] A,
  input  [7:0] B,
  input  C_in,
  output [7:0] Res,
  output C_out
);

  wire n4bitadder_2_c_out;

  _4BitAdder u_4bitadder_1 (.A(A[7:4]), .B(B[7:4]), .C_in(n4bitadder_2_c_out), .Res(Res[7:4]), .C_out(C_out));
  _4BitAdder u_4bitadder_2 (.A(A[3:0]), .B(B[3:0]), .C_in(C_in), .Res(Res[3:0]), .C_out(n4bitadder_2_c_out));
endmodule

module _32BitAdder (
  input  [31:0] A,
  input  [31:0] B,
  input  C_in,
  output [31:0] Res,
  output Overflow
);

  wire n8bitadder_2_c_out, n8bitadder_3_c_out, n8bitadder_4_c_out;

  _8BitAdder u_8bitadder_1 (.A(A[31:24]), .B(B[31:24]), .C_in(n8bitadder_2_c_out), .Res(Res[31:24]), .C_out(Overflow));
  _8BitAdder u_8bitadder_2 (
    .A(A[23:16]), .B(B[23:16]), .C_in(n8bitadder_3_c_out), .Res(Res[23:16]), .C_out(n8bitadder_2_c_out));
  _8BitAdder u_8bitadder_3 (
    .A(A[15:8]), .B(B[15:8]), .C_in(n8bitadder_4_c_out), .Res(Res[15:8]), .C_out(n8bitadder_3_c_out));
  _8BitAdder u_8bitadder_4 (.A(A[7:0]), .B(B[7:0]), .C_in(C_in), .Res(Res[7:0]), .C_out(n8bitadder_4_c_out));
endmodule
