// Logisim project Shifter32.circ as structural Verilog: 8 circuits, main circuit main
module main (
  input  [31:0] in_1,
  input  [4:0] in_2,
  input  [1:0] in_3,
  output [31:0] out_4
);

  wire [31:0] bit_reverser_1_out_2, bit_reverser_2_out_2, multiplexer_1_out, multiplexer_2_out,
       multiplexer_3_out, not_1_out, not_2_out, sll32_1_out_3;

  Bit_Reverser bit_reverser_1 (.in_1(in_1), .out_2(bit_reverser_1_out_2));
  assign not_1_out = ~bit_reverser_1_out_2;  // NOT_Gate not_1, 32 bits wide
  Multiplexer #(.width(32)) multiplexer_1 (
    .in0(in_1), .in1(multiplexer_2_out), .out(multiplexer_1_out), .sel(in_3[0]));  // open: en
  Multiplexer #(.width(32)) multiplexer_2 (
    .in0(bit_reverser_1_out_2), .in1(not_1_out), .out(multiplexer_2_out), .sel(in_3[1]));  // open: en
  SLL32 sll32_1 (.in_1(multiplexer_1_out), .in_2(in_2), .out_3(sll32_1_out_3));
  assign not_2_out = ~sll32_1_out_3;  // NOT_Gate not_2, 32 bits wide
  Multiplexer #(.width(32)) multiplexer_3 (
    .in0(sll32_1_out_3), .in1(not_2_out), .out(multiplexer_3_out), .sel(in_3[1]));  // open: en
  Multiplexer #(.width(32)) multiplexer_4 (
    .in0(multiplexer_3_out), .in1(bit_reverser_2_out_2), .out(out_4), .sel(in_3[0]));  // open: en
  Bit_Reverser bit_reverser_2 (.in_1(multiplexer_3_out), .out_2(bit_reverser_2_out_2));

  // Notes on the sheet:
  //   00 for SLL, 01 for SRL, 11 for SRA
endmodule

module SLL1 (
  input  [31:0] in_1,
  output [31:0] out_2
);


  assign out_2 = {in_1[30:0], 1'b0};
endmodule

module SLL2 (
  input  [31:0] in_1,
  output [31:0] out_2
);


  assign out_2 = {in_1[29:0], 2'b00};
endmodule

module SLL4 (
  input  [31:0] in_1,
  output [31:0] out_2
);


  assign out_2 = {in_1[27:0], 4'b0000};
endmodule

module SLL8 (
  input  [31:0] in_1,
  output [31:0] out_2
);


  assign out_2 = {in_1[23:0], {8{1'b0}}};
endmodule

module SLL16 (
  input  [31:0] in_1,
  output [31:0] out_2
);


  assign out_2 = {in_1[15:0], {16{1'b0}}};
endmodule

module SLL32 (
  input  [31:0] in_1,
  input  [4:0] in_2,
  output [31:0] out_3
);

  wire [31:0] multiplexer_1_out, multiplexer_2_out, multiplexer_3_out, multiplexer_4_out, sll1_1_out_2,
       sll2_1_out_2, sll4_1_out_2, sll8_1_out_2, sll16_1_out_2;

  SLL16 sll16_1 (.in_1(in_1), .out_2(sll16_1_out_2));
  Multiplexer #(.width(32)) multiplexer_1 (
    .in0(in_1), .in1(sll16_1_out_2), .out(multiplexer_1_out), .sel(in_2[4]));  // open: en
  Multiplexer #(.width(32)) multiplexer_2 (
    .in0(multiplexer_1_out), .in1(sll8_1_out_2), .out(multiplexer_2_out), .sel(in_2[3]));  // open: en
  SLL8 sll8_1 (.in_1(multiplexer_1_out), .out_2(sll8_1_out_2));
  SLL4 sll4_1 (.in_1(multiplexer_2_out), .out_2(sll4_1_out_2));
  Multiplexer #(.width(32)) multiplexer_3 (
    .in0(multiplexer_2_out), .in1(sll4_1_out_2), .out(multiplexer_3_out), .sel(in_2[2]));  // open: en
  SLL2 sll2_1 (.in_1(multiplexer_3_out), .out_2(sll2_1_out_2));
  Multiplexer #(.width(32)) multiplexer_4 (
    .in0(multiplexer_3_out), .in1(sll2_1_out_2), .out(multiplexer_4_out), .sel(in_2[1]));  // open: en
  SLL1 sll1_1 (.in_1(multiplexer_4_out), .out_2(sll1_1_out_2));
  Multiplexer #(.width(32)) multiplexer_5 (
    .in0(multiplexer_4_out), .in1(sll1_1_out_2), .out(out_3), .sel(in_2[0]));  // open: en
endmodule

module Bit_Reverser (
  input  [31:0] in_1,
  output [31:0] out_2
);


  assign out_2 = {in_1[0], in_1[1], in_1[2], in_1[3], in_1[4], in_1[5], in_1[6], in_1[7], in_1[8], in_1[9], in_1[10], in_1[11], in_1[12], in_1[13], in_1[14], in_1[15], in_1[16], in_1[17], in_1[18], in_1[19], in_1[20], in_1[21], in_1[22], in_1[23], in_1[24], in_1[25], in_1[26], in_1[27], in_1[28], in_1[29], in_1[30], in_1[31]};
endmodule
