// Logisim project fsm.circ as structural Verilog: 4 circuits, main circuit main
module main (
  input  in_1,
  input  in_2,
  output out_3,
  output out_4
);

  wire clock_1_out, clock_2_out, mealy_combinational_circuit_1_out_4, register_1_q;
  wire [1:0] moore_input_comb_1_out_3, register_2_q;

  Mealy_Combinational_Circuit mealy_combinational_circuit_1 (
    .in_1(in_1), .out_4(mealy_combinational_circuit_1_out_4), .out_3(out_3), .in_2(register_1_q));
  Clock clock_1 (.out(clock_1_out));
  Moore_Input_Comb moore_input_comb_1 (.in_1(in_2), .in_2(register_2_q), .out_3(moore_input_comb_1_out_3));
  Clock clock_2 (.out(clock_2_out));
  Register #(.width(1)) register_1 (
    .D(mealy_combinational_circuit_1_out_4), .Q(register_1_q), .clk(clock_1_out));  // open: en, clr
  Register #(.width(2)) register_2 (
    .D(moore_input_comb_1_out_3), .Q(register_2_q), .clk(clock_2_out));  // open: en, clr
  Moore_Output_Comb moore_output_comb_1 (.in_1(register_2_q), .out_2(out_4));
endmodule

module Mealy_Combinational_Circuit (
  input  in_1,
  input  in_2,
  output out_3,
  output out_4
);

  xor xor_1 (out_3, in_1, in_2);

  assign out_4 = in_1;
endmodule

module Moore_Input_Comb (
  input  in_1,
  input  [1:0] in_2,
  output [1:0] out_3
);


  assign out_3 = {in_2[0], in_1};
endmodule

module Moore_Output_Comb (
  input  [1:0] in_1,
  output out_2
);

  xor xor_1 (out_2, in_1[0], in_1[1]);
endmodule
