// Logisim project counter_4_bit.circ as structural Verilog: 1 circuit, main circuit main
module main (
  input  Reset
);

  wire Clk_out;
  wire [3:0] counter_1_q;

  Clock Clk (.out(Clk_out));
  Counter #(.width(4), .max('hf)) counter_1 (
    .count(1'b1), .Q(counter_1_q), .clk(Clk_out), .clr(Reset));  // open: load, D, carry
  Hex_Digit_Display hex_digit_display_1 (.value(counter_1_q));  // open: dp
endmodule
