// Logisim project gcd.circ as structural Verilog: 3 circuits, main circuit main
module main (
  input  [7:0] A,
  input  [7:0] B,
  input  Load,
  output [7:0] Output,
  output Result_calculated
);

  wire Clk_out, comparator_1_gt, not_1_out, or_1_out, or_2_out;
  wire [7:0] multiplexer_1_out, multiplexer_2_out, multiplexer_3_out, multiplexer_4_out, register_1_q,
       register_2_q, subtractor_1_out, subtractor_2_out;

  Clock Clk (.out(Clk_out));
  Multiplexer #(.width(8)) multiplexer_1 (
    .in0(register_1_q), .in1(subtractor_1_out), .out(multiplexer_1_out), .sel(or_1_out));  // open: en
  Multiplexer #(.width(8)) multiplexer_2 (
    .in0(multiplexer_1_out), .in1(A), .out(multiplexer_2_out), .sel(Load));  // open: en
  Multiplexer #(.width(8)) multiplexer_3 (
    .in0(subtractor_2_out), .in1(register_2_q), .out(multiplexer_3_out), .sel(or_1_out));  // open: en
  Multiplexer #(.width(8)) multiplexer_4 (
    .in0(multiplexer_3_out), .in1(B), .out(multiplexer_4_out), .sel(Load));  // open: en
  or or_1 (or_1_out, Result_calculated, comparator_1_gt);
  Register register_1 (.D(multiplexer_2_out), .en(or_2_out), .Q(register_1_q), .clk(Clk_out));  // open: clr
  Register register_2 (.D(multiplexer_4_out), .en(or_2_out), .Q(register_2_q), .clk(Clk_out));  // open: clr
  or or_2 (or_2_out, Load, not_1_out);
  not not_1 (not_1_out, or_1_out);
  Comparator comparator_1 (.a(subtractor_2_out), .b(register_2_q), .gt(comparator_1_gt));  // open: eq, lt
  Subtractor subtractor_1 (.a(register_1_q), .b(register_2_q), .out(subtractor_1_out));  // open: bin, bout
  Subtractor subtractor_2 (.a(register_2_q), .b(register_1_q), .out(subtractor_2_out));  // open: bin, bout
  Multiplexer #(.width(8)) multiplexer_5 (
    .in0({8{1'b0}}), .in1(register_1_q), .out(Output), .sel(Result_calculated));  // open: en
  Comparator comparator_2 (.a(subtractor_1_out), .b(subtractor_2_out), .eq(Result_calculated));  // open: gt, lt
endmodule

module _8_Bit_Not_Equal (
  input  [7:0] in_1,
  input  [7:0] in_2,
  output out_3
);

  wire [7:0] xor_1_out;

  assign xor_1_out = in_1 ^ in_2;  // XOR_Gate xor_1, 8 bits wide
  or or_1 (out_3, xor_1_out[0], xor_1_out[1], xor_1_out[2], xor_1_out[3], xor_1_out[5], xor_1_out[6], xor_1_out[7], xor_1_out[4]);
endmodule

module _8_Bit_Less_than (
  input  [7:0] in_1,
  input  [7:0] in_2,
  output out_3
);

  Subtractor subtractor_1 (.a(in_1), .b(in_2), .bout(out_3));  // open: out, bin
endmodule
