// Logisim project foo_circuit.circ as structural Verilog: 1 circuit, main circuit main
module main (
  input  [15:0] Input,
  input  Reset,
  output Calculated,
  output [15:0] Output
);

  wire Clock_out;
  wire [15:0] adder_1_out, counter_1_q, multiplexer_1_out;

  Clock Clock (.out(Clock_out));
  Counter #(.width(16), .max('hffff)) counter_1 (
    .Q(counter_1_q), .clk(Clock_out), .clr(Reset));  // open: load, D, count, carry
  Multiplexer #(.width(16)) multiplexer_1 (
    .in0(counter_1_q), .in1({16{1'b0}}), .out(multiplexer_1_out), .sel(Calculated));  // open: en
  Comparator #(.width(16)) comparator_1 (.a(Input), .b(counter_1_q), .lt(Calculated));  // open: gt, eq
  Adder #(.width(16)) adder_1 (.a(Output), .b(multiplexer_1_out), .out(adder_1_out));  // open: cin, cout
  Register #(.width(16)) register_1 (.D(adder_1_out), .Q(Output), .clk(Clock_out), .clr(Reset));  // open: en
endmodule
